// Logisim project alu-control.circ as structural Verilog: 3 circuits, main circuit main
module main (
  input  [1:0] Opcode,
  input  [5:0] Funct,
  input  [1:0] sh,
  output [3:0] ALUControl
);

  wire funct_separated_1_i, If_1101_output;
  wire [3:0] funct_separated_1_cmd, multiplexer_1_out, multiplexer_2_out, rom_1_data;

  // Probe on funct_separated_1_cmd
  funct_separated funct_separated_1 (.in_1(Funct), .cmd(funct_separated_1_cmd), .I(funct_separated_1_i));
  // Probe on funct_separated_1_i
  If_1101 If_1101 (.sh(Opcode), .cmd(funct_separated_1_cmd), .\output (If_1101_output));
  Multiplexer #(.select(2), .width(4), .enable("false")) multiplexer_1 (
    .in0(4'b0100), .in1(4'b0101), .in2(4'b0110), .out(multiplexer_1_out), .sel(sh));  // open: in3
  ROM #(.addrWidth(4), .dataWidth(4)) rom_1 (.addr(funct_separated_1_cmd), .data(rom_1_data));  // open: sel
  Multiplexer #(.width(4), .enable("false")) multiplexer_2 (
    .in0(rom_1_data), .in1(multiplexer_1_out), .out(multiplexer_2_out), .sel(If_1101_output));
  Multiplexer #(.select(2), .width(4), .enable("false")) multiplexer_3 (
    .in0(multiplexer_2_out), .in1(4'b0111), .in2(4'b0111), .out(ALUControl), .sel(Opcode));  // open: in3
  // Probe on ALUControl

  // Notes on the sheet:
  //   I
  //   cmd
  //   S
  //   sh code
  //   contents of rom_1 (hex, n*v repeats v):
  //   0 2 8 0 7 7 8 0 0 0 8 0 1 0 0 3
  //   if 1101
  //   DO NOT MOVE, CHANGE, ADD, OR REMOVE INPUTS AND OUTPUTS!!!
  //   op code
  //   and
  //   or
  //   xor
  //   not
  //   lsl
  //   lsr
  //   asr
  //   add
  //   sub
endmodule

module funct_separated (
  input  [5:0] in_1,
  output [3:0] cmd,
  output I
);

  wire [5:0] shifter_1_out;

  Shifter #(.width(6), .shift("lr")) shifter_1 (.in(in_1), .\dist (3'b001), .out(shifter_1_out));
  BitSelector #(.width(6)) bitselector_1 (.in(in_1), .out(I), .sel(3'b101));
  BitSelector #(.width(6), .group(4)) bitselector_2 (.in(shifter_1_out), .out(cmd), .sel(1'b0));

  // Notes on the sheet:
  //   funct
endmodule

module If_1101 (
  input  [1:0] sh,
  input  [3:0] cmd,
  output \output 
);

  wire comparator_1_eq, comparator_2_eq;

  Comparator #(.width(2)) comparator_1 (.a(sh), .b(2'b00), .eq(comparator_1_eq));  // open: gt, lt
  Comparator #(.width(4)) comparator_2 (.a(cmd), .b(4'b1101), .eq(comparator_2_eq));  // open: gt, lt
  and and_1 (\output , comparator_1_eq, comparator_2_eq);
endmodule
