// Logisim project cpu.circ as structural Verilog: 1 circuit, main circuit main
module main (
  input  [31:0] INSTRUCTION,
  input  CLOCK,
  output [31:0] FETCH_ADDRESS,
  output [31:0] R0_Value,
  output [31:0] R1_Value,
  output [31:0] R2_Value,
  output [31:0] LR_Value,
  output [31:0] SP_Value
);

  wire main_3_p1;
  wire [3:0] ALU_Control_alucontrol;
  wire [4:4] undriven;
  wire [31:0] adder_1_out, bit_extender_1_out, bit_extender_2_out, main_1_p4, main_1_p11, main_1_p12,
       main_2_result, main_3_p5, multiplexer_1_out, multiplexer_3_out, shifter_1_out;

  Register #(.width(32)) PC (.D(adder_1_out), .Q(FETCH_ADDRESS), .clk(CLOCK));  // open: en, clr
  Adder #(.width(32)) adder_1 (.a(FETCH_ADDRESS), .b(32'h4), .out(adder_1_out));  // open: cin, cout
  alu_control_main ALU_Control (
    .Opcode(INSTRUCTION[27:26]), .Funct(INSTRUCTION[25:20]), .sh(INSTRUCTION[6:5]),
    .ALUControl(ALU_Control_alucontrol));
  assign bit_extender_1_out = {{24{1'b0}}, INSTRUCTION[7:0]};  // Bit_Extender bit_extender_1
  assign bit_extender_2_out = {{20{1'b0}}, INSTRUCTION[11:0]};  // Bit_Extender bit_extender_2
  Shifter #(.width(32), .shift("rr")) shifter_1 (
    .in(bit_extender_1_out), .\dist ({undriven[4], INSTRUCTION[11:8]}), .out(shifter_1_out));
  // regfile_main main_1: pin names not known; wires that end beside it: INSTRUCTION[19:16], INSTRUCTION[3:0], INSTRUCTION[15:12], main_1_p4, R0_Value, R1_Value, R2_Value, CLOCK, LR_Value, SP_Value, main_1_p11, main_1_p12
  Multiplexer #(.width(32), .enable("false")) multiplexer_1 (
    .in0(shifter_1_out), .in1(bit_extender_2_out), .out(multiplexer_1_out), .sel(INSTRUCTION[25]));
  Multiplexer #(.width(32), .enable("false")) multiplexer_2 (
    .in0(main_2_result), .in1(main_3_p5), .out(main_1_p4));  // open: sel
  Multiplexer #(.width(32), .enable("false")) multiplexer_3 (
    .in0(main_1_p12), .in1(multiplexer_1_out), .out(multiplexer_3_out));  // open: sel
  alu_main main_2 (
    .ALUControl(ALU_Control_alucontrol), .A(main_1_p11), .Result(main_2_result), .B(multiplexer_3_out));  // open: ALUFlags
  // mem_main main_3: pin names not known; wires that end beside it: main_3_p1, main_2_result, main_3_p1, CLOCK, main_3_p5
  // Pins of 4 and 5 bits meet at {undriven[4], INSTRUCTION[11:8]}

  // Other names for the same wires on the sheet: clk = CLOCK; fetch_addr[31:0] = FETCH_ADDRESS; R0[31:0] = R0_Value;
  //   R1[31:0] = R1_Value; R2[31:0] = R2_Value; R13[31:0] = SP_Value; R14[31:0] = LR_Value

  // Notes on the sheet:
  //   Output
  //   Inputs
  //   rot
  //   Rn
  //   Rm
  //   Rd
  //   RegWrite
  //   These are DEBUG/TEST outputs from your circuit.
  //   I
  //   memToReg
  //   ALU Src (isLDR)
  //   MemWrite
endmodule
