// Logisim project cpu.circ as structural Verilog: 3 circuits, main circuit main
module main (
  input  [31:0] INSTRUCTION,
  input  CLOCK,
  output [31:0] FETCH_ADDRESS,
  output [31:0] R0_Value,
  output [31:0] R1_Value,
  output [31:0] R2_Value,
  output [31:0] LR_Value,
  output [31:0] SP_Value
);

  wire ALUSrc, control_1_i, MemToReg, MemWrite, PCSrc, RegWrite;
  wire [1:0] control_1_op;
  wire [3:0] ALU_Control_alucontrol, cond, control_1_rd, control_1_rn;
  wire [4:0] bit_extender_1_out;
  wire [5:0] control_1_funct;
  wire [11:0] control_1_src2;
  wire [31:0] adder_1_out, bit_extender_2_out, bit_extender_3_out, main_1_p4, main_1_p12, main_1_p13,
       main_2_result, main_3_p5, multiplexer_1_out, multiplexer_3_out, shifter_1_out;

  Register #(.width(32)) PC (.D(adder_1_out), .Q(FETCH_ADDRESS), .clk(CLOCK));  // open: en, clr
  Adder #(.width(32)) adder_1 (.a(FETCH_ADDRESS), .b(32'h4), .out(adder_1_out));  // open: cin, cout
  CONTROL control_1 (
    .Instruction(INSTRUCTION), .cond(cond), .op(control_1_op), .funct(control_1_funct), .MemToReg(MemToReg),
    .Src2(control_1_src2), .MemWrite(MemWrite), .Rd(control_1_rd), .ALUSrc(ALUSrc), .Rn(control_1_rn),
    .RegWrite(RegWrite), .PCSrc(PCSrc), .I(control_1_i));
  alu_control_main ALU_Control (
    .Opcode(control_1_op), .Funct(control_1_funct), .sh(control_1_src2[6:5]),
    .ALUControl(ALU_Control_alucontrol));
  assign bit_extender_1_out = {{1{1'b0}}, control_1_src2[11:8]};  // Bit_Extender bit_extender_1
  assign bit_extender_2_out = {{24{1'b0}}, control_1_src2[7:0]};  // Bit_Extender bit_extender_2
  assign bit_extender_3_out = {{20{1'b0}}, control_1_src2};  // Bit_Extender bit_extender_3
  Shifter #(.width(32), .shift("rr")) shifter_1 (
    .in(bit_extender_2_out), .\dist (bit_extender_1_out), .out(shifter_1_out));
  // regfile_main main_1: pin names not known; wires that end beside it: control_1_rn, control_1_src2[3:0], control_1_rd, main_1_p4, R0_Value, R1_Value, RegWrite, R2_Value, CLOCK, LR_Value, SP_Value, main_1_p12, main_1_p13
  Multiplexer #(.width(32), .enable("false")) multiplexer_1 (
    .in0(shifter_1_out), .in1(bit_extender_3_out), .out(multiplexer_1_out), .sel(control_1_i));
  Multiplexer #(.width(32), .enable("false")) multiplexer_2 (
    .in0(main_2_result), .in1(main_3_p5), .out(main_1_p4), .sel(MemToReg));
  Multiplexer #(.width(32), .enable("false")) multiplexer_3 (
    .in0(main_1_p13), .in1(multiplexer_1_out), .out(multiplexer_3_out), .sel(ALUSrc));
  alu_main main_2 (
    .ALUControl(ALU_Control_alucontrol), .A(main_1_p12), .Result(main_2_result), .B(multiplexer_3_out));  // open: ALUFlags
  // mem_main main_3: pin names not known; wires that end beside it: main_2_result, main_1_p13, MemWrite, CLOCK, main_3_p5

  // Other names for the same wires on the sheet: clk = CLOCK; fetch_addr[31:0] = FETCH_ADDRESS; R0[31:0] = R0_Value;
  //   R1[31:0] = R1_Value; R2[31:0] = R2_Value; R13[31:0] = SP_Value; R14[31:0] = LR_Value

  // Notes on the sheet:
  //   Output
  //   Inputs
  //   Src2
  //   I
  //   imm8
  //   rot
  //   Rm
  //   sh
  //   Rn
  //   Rm
  //   Rd
  //   These are DEBUG/TEST outputs from your circuit.
endmodule

module CONTROL (
  input  [31:0] Instruction,
  output [3:0] cond,
  output [1:0] op,
  output [5:0] funct,
  output MemToReg,
  output [11:0] Src2,
  output MemWrite,
  output [3:0] Rd,
  output ALUSrc,
  output [3:0] Rn,
  output RegWrite,
  output PCSrc,
  output I
);

  mov mov_1 (
    .op1(Instruction[26]), .op2(Instruction[27]), .I(Instruction[25]), .L(Instruction[20]),
    .RegWrite(RegWrite), .immSrcI(I), .ALUSrc(ALUSrc), .MemWrite(MemWrite), .MemToReg(MemToReg), .PCSrc(PCSrc));

  assign cond = Instruction[31:28];
  assign funct = Instruction[25:20];
  assign op = Instruction[27:26];
  assign Rd = Instruction[15:12];
  assign Rn = Instruction[19:16];
  assign Src2 = Instruction[11:0];

  // Notes on the sheet:
  //   Src2
  //   Rd
  //   Rn
  //   funct
  //   op
  //   cond
endmodule

module mov (
  input  op1,
  input  op2,
  input  I,
  input  L,
  output RegWrite,
  output immSrcI,
  output ALUSrc,
  output MemWrite,
  output MemToReg,
  output PCSrc
);


  assign ALUSrc = 1'b1;
  assign immSrcI = 1'b1;
  assign MemToReg = 1'b0;
  assign MemWrite = 1'b0;
  assign RegWrite = 1'b1;
endmodule
